# Fritzing sketch Pablo (saved by Fritzing 0.8.7b)
breadboards: 1

parts:
  BATT1 = LiPoly Battery (1300mAh)
  BB1 = 4-Line Bi-Directional Level Shifter
  SPKR1 = Loudspeaker
  Arduino1 = Arduino Uno (Rev3)
  J1 = Basic Servo
  J2 = Basic Servo
  neopixel1 = Neopixel Ring 16
  neopixel2 = Neopixel Ring 12
  BLUEFRUIT1 = Adafruit Bluefruit EZ-LINK v1.0
  TRINKET1 = Trinket 3V
  Emic1 = Emic 2 [package="SIP (Single Inline) [THT]"]

nets:
  N1: BATT1.positive, TRINKET1.no_name_yet#1
  GND: BATT1.negative, BB1.GND#6, neopixel1.GND, neopixel2.GND, TRINKET1.no_name_yet#2
  N2: BB1.LV, TRINKET1.no_name_yet#6
  N3: BB1.A1, TRINKET1.no_name_yet#9
  N4: BB1.A2, TRINKET1.no_name_yet#7
  5V: BB1.HV, Arduino1.5V, J1.vcc, J2.vcc, BLUEFRUIT1.Vin, Emic1.5V
  N5: BB1.B1, Arduino1.A4/SDA
  N6: BB1.B2, Arduino1.A5/SCL
  GND_2: BB1.GND#16, Arduino1.GND, J1.gnd, J2.gnd, BLUEFRUIT1.GND, Emic1.GND
  N7: SPKR1.pin1, Emic1.SP-
  N8: SPKR1.pin2, Emic1.SP+
  N9: Arduino1.D9_PWM, J1.pulse
  N10: Arduino1.D10_PWM/SS, J2.pulse
  N11: Arduino1.D0/RX, BLUEFRUIT1.TX
  N12: Arduino1.D1/TX, BLUEFRUIT1.RX
  N13: Arduino1.D5_PWM, Emic1.SOUT
  N14: Arduino1.D6_PWM, Emic1.SIN
  N15: Arduino1.RESET, BLUEFRUIT1.DTR
  N16: neopixel1.IN, TRINKET1.no_name_yet#3
  N17: neopixel1.OUT, neopixel2.IN

custom parts:
  LiPoly Battery (1300mAh): Lithium Ion Polymer Battery (1300mAh)
  4-Line Bi-Directional Level Shifter: 4-Channel Bi-Directional Level Shifter
  Neopixel Ring 16: Neopixel Ring x16
  Neopixel Ring 12: Neopixel Ring x12
  Adafruit Bluefruit EZ-LINK v1.0: Bluefruit EZ-LINK, Bluetooth Serial Link & Arduino Programmer
  Trinket 3V: Adafruit Trinket 3V
  Emic 2: Emic 2 Text to Speech Module
